// Logisim project CS1501_U201514477_华龙_cpu.circ as structural Verilog: 3 circuits, main circuit MIPS CPU
module MIPS_CPU (
);

  wire ALU_Equal, and_1_out, and_2_out, beq, bne, branch, clk, Din__DM, Din__DM_half, Din__PC_1, extend_IMM,
       extend_shamt, jump, jump_register, rA___v0, rB___a0, rW__GPR_31, rW__rd, WE, X__RF_B, Y__RF_A,
       Y__S_EXT, zero_ext_IMM;
  wire [3:0] ALUOP;
  wire [4:0] multiplexer_4_out, multiplexer_5_out, multiplexer_6_out, multiplexer_7_out;
  wire [5:0] Funct, OP;
  wire [15:0] multiplexer_17_out;
  wire [16:0] multiplexer_8_out, multiplexer_9_out, multiplexer_10_out;
  wire [25:6] rom_1_data;
  wire [31:0] adder_1_out, alu_1_result, bit_extender_1_out, mips_ram_1_p5, multiplexer_1_out,
       multiplexer_2_out, multiplexer_3_out, multiplexer_11_out, multiplexer_12_out, multiplexer_13_out,
       multiplexer_15_out, multiplexer_16_out, PC, PC_1, pull_resistor_1_node, RF_A, RF_B;

  Multiplexer #(.width(32), .enable("false")) multiplexer_1 (
    .in0(multiplexer_2_out), .in1(multiplexer_3_out), .out(multiplexer_1_out), .sel(jump));
  Multiplexer #(.width(32), .enable("false")) multiplexer_2 (
    .in0(PC_1), .in1(adder_1_out), .out(multiplexer_2_out), .sel(branch));
  Multiplexer #(.width(32), .enable("false")) multiplexer_3 (
    .in0({PC_1[31:28], OP[1:0], rom_1_data, Funct[5:2], 2'b00}), .in1(RF_A), .out(multiplexer_3_out),
    .sel(jump_register));
  PC_1 pc_1_1 (.PC(PC), .PC_4(PC_1));
  Register #(.width(32)) u_PC (.D(multiplexer_1_out), .Q(PC), .clk(clk));  // open: en, clr
  ROM #(.addrWidth(24), .dataWidth(32)) rom_1 (.addr(PC[25:2]), .data({OP, rom_1_data, Funct}));  // open: sel
  Multiplexer #(.width(5), .enable("false")) multiplexer_4 (
    .in0(rom_1_data[20:16]), .in1(rom_1_data[15:11]), .out(multiplexer_4_out), .sel(rW__rd));
  Multiplexer #(.width(5), .enable("false")) multiplexer_5 (
    .in0(rom_1_data[25:21]), .in1(5'b00010), .out(multiplexer_5_out), .sel(rA___v0));
  Multiplexer #(.width(5), .enable("false")) multiplexer_6 (
    .in0(rom_1_data[20:16]), .in1(5'b00100), .out(multiplexer_6_out), .sel(rB___a0));
  Multiplexer #(.width(5), .enable("false")) multiplexer_7 (
    .in0(multiplexer_4_out), .in1({5{1'b1}}), .out(multiplexer_7_out), .sel(rW__GPR_31));
  Multiplexer #(.width(17), .enable("false")) multiplexer_8 (
    .in0({{12{1'b0}}, rom_1_data[10:6]}), .in1(17'ha), .out(multiplexer_8_out), .sel(extend_shamt));
  Multiplexer #(.width(17), .enable("false")) multiplexer_9 (
    .in0(multiplexer_8_out), .in1(multiplexer_10_out), .out(multiplexer_9_out), .sel(extend_IMM));
  Multiplexer #(.width(17), .enable("false")) multiplexer_10 (
    .in0({{2{rom_1_data[15]}}, rom_1_data[14:6], Funct}), .in1({1'b0, rom_1_data[15:6], Funct}),
    .out(multiplexer_10_out), .sel(zero_ext_IMM));
  and and_1 (and_1_out, beq, ALU_Equal);
  or or_1 (branch, and_1_out, and_2_out);
  and and_2 (and_2_out, ~ALU_Equal, bne);  // AND_Gate
  Multiplexer #(.width(32), .enable("false")) multiplexer_11 (
    .in0(alu_1_result), .in1(PC_1), .out(multiplexer_11_out), .sel(Din__PC_1));
  Multiplexer #(.width(32), .enable("false")) multiplexer_12 (
    .in0(multiplexer_11_out), .in1(multiplexer_13_out), .out(multiplexer_12_out), .sel(Din__DM));
  Multiplexer #(.width(32), .enable("false")) multiplexer_13 (
    .in0(mips_ram_1_p5), .in1({{16{1'b0}}, multiplexer_17_out}), .out(multiplexer_13_out), .sel(Din__DM_half));
  assign bit_extender_1_out = {{15{multiplexer_9_out[16]}}, multiplexer_9_out};  // Bit_Extender bit_extender_1
  // RegisterFile registerfile_1: pin names not known; wires that end beside it: multiplexer_12_out, clk, WE, multiplexer_7_out, multiplexer_5_out, multiplexer_6_out, RF_A, RF_B
  Pull_Resistor pull_resistor_1 (.node(pull_resistor_1_node));
  Multiplexer #(.width(32), .enable("false")) multiplexer_14 (
    .in0(RF_A), .in1(RF_B), .out(pull_resistor_1_node), .sel(X__RF_B));
  Multiplexer #(.width(32), .enable("false")) multiplexer_15 (
    .in0(RF_B), .in1(RF_A), .out(multiplexer_15_out), .sel(Y__RF_A));
  Multiplexer #(.width(32), .enable("false")) multiplexer_16 (
    .in0(multiplexer_15_out), .in1(bit_extender_1_out), .out(multiplexer_16_out), .sel(Y__S_EXT));
  Pull_Resistor pull_resistor_2 (.node(multiplexer_16_out));
  Pull_Resistor #(.pull(1)) pull_resistor_3 (.node(ALUOP));
  // MIPS_RAM mips_ram_1: pin names not known; wires that end beside it: alu_1_result[25:2], RF_B, rA___v0, clk, mips_ram_1_p5
  Adder #(.width(32)) adder_1 (.a(PC), .b({bit_extender_1_out[29:0], 2'b00}), .out(adder_1_out));  // open: cin, cout
  ALU alu_1 (
    .AluOP(ALUOP), .X(pull_resistor_1_node), .Equal(ALU_Equal), .Result(alu_1_result), .Y(multiplexer_16_out));  // open: Signed_Overflow, Result_2, UnSigned_Overflow
  Multiplexer #(.width(16), .enable("false")) multiplexer_17 (
    .in0(mips_ram_1_p5[15:0]), .in1(mips_ram_1_p5[31:16]), .out(multiplexer_17_out), .sel(alu_1_result[1]));
endmodule

module PC_1 (
  input  [31:0] PC,
  output [31:0] PC_4
);

  // Incrementer incrementer_1: pin names not known; wires that end beside it: PC[31:2], PC_4[31:2]

  assign PC_4[1:0] = PC[1:0];
endmodule

module \_8位数码管显示  (
);

  wire [31:0] undriven, \数码管锁存_q ;

  Register #(.width(32)) \u_数码管锁存  (.D(undriven), .Q(\数码管锁存_q ));  // open: en, clk, clr
  Hex_Digit_Display hex_digit_display_1 (.value(\数码管锁存_q [31:28]));  // open: dp
  Hex_Digit_Display hex_digit_display_2 (.value(\数码管锁存_q [27:24]));  // open: dp
  Hex_Digit_Display hex_digit_display_3 (.value(\数码管锁存_q [23:20]));  // open: dp
  Hex_Digit_Display hex_digit_display_4 (.value(\数码管锁存_q [19:16]));  // open: dp
  Hex_Digit_Display hex_digit_display_5 (.value(\数码管锁存_q [11:8]));  // open: dp
  Hex_Digit_Display hex_digit_display_6 (.value(\数码管锁存_q [15:12]));  // open: dp
  Hex_Digit_Display hex_digit_display_7 (.value(\数码管锁存_q [3:0]));  // open: dp
  Hex_Digit_Display hex_digit_display_8 (.value(\数码管锁存_q [7:4]));  // open: dp
endmodule
